# Fritzing sketch ledOnOff (saved by Fritzing 0.9.3b)

parts:
  Part1 = Arduino Uno (Rev3)
  LED1 = LED - 5mm [color="Red (633nm)" package="5 mm [THT]"]
  R1 = Resistor [tolerance=±5% resistance=120 package="0603 [SMD]"]

nets:
  N1: Part1.D10_PWM/SS, LED1.anode
  N2: Part1.GND, R1.Pin_0
