# Fritzing sketch lightBulbsOnOff (saved by Fritzing 0.9.3b)

parts:
  Part1 = Arduino Uno (Rev3)
  Modulo_Relay = Keyes Relay [package=THT]
  Power_plug1 = Power plug
  LED1 = LEDs [package=led10mm]

nets:
  N1: Part1.D5_PWM, Modulo_Relay.signal
  N2: Part1.D7, Modulo_Relay.ground
  N3: Part1.GND, Modulo_Relay.power
  N4: Modulo_Relay.C, Power_plug1.VCC
  N5: Modulo_Relay.NO, LED1.A
  N6: Power_plug1.GND, LED1.C

custom parts:
  Keyes Relay: The Keyes 5V relay module is suitable for SCM development, home appliance control. It uses a 5V~12V TIL control signal which can control DC / AC signal.
  LEDs: LEDs Standard schematic elements and footprints for 5mm, 3mm, 1206, and 0603 sized LEDs. 5mm - Spark Fun Electronics SKU : COM-00529 (and others)
